# Fritzing sketch Esquema_Medidor_TU_Ender3 (saved by Fritzing 0.9.3b)

parts:
  Launchpad1 = TI Launchpad MSP430G2
  LCD1 = LCD screen
  R1 = Resistor [tolerance=±5% resistance=4.7k package=THT]
  DHT11 = Humidity and Temperature Sensor DHT11

nets:
  N1: Launchpad1.p7, LCD1.R/W
  N2: Launchpad1.p6, LCD1.RS
  N3: Launchpad1.p5, LCD1.DB7
  N4: Launchpad1.p4, LCD1.DB6
  N5: Launchpad1.p3, LCD1.DB5
  N6: Launchpad1.p2, LCD1.DB4
  N7: Launchpad1.p1, DHT11.Vcc
  N8: Launchpad1.p11, DHT11.Data-signal
  N9: Launchpad1.p14, LCD1.E
  N10: Launchpad1.p20, DHT11.GND_2
  N11: LCD1.VSS, R1.Pin_1
  N12: LCD1.V0, R1.Pin_0

custom parts:
  Humidity and Temperature Sensor DHT11: Digital relative humidity & temperature sensor DHT11
